// Logisim project ETFStudent.circ as structural Verilog: 2 circuits, main circuit KMADR
module KMADR (
  input  immed,
  input  memdir,
  input  memind,
  input  regind,
  input  postincr,
  input  postdec,
  input  regdir,
  output [4:0] Adr
);

  assign Adr = immed ? 5'b00010 : 5'bz;  // Controlled_Buffer controlled_buffer_1
  assign Adr = memdir ? 5'b00100 : 5'bz;  // Controlled_Buffer controlled_buffer_2
  assign Adr = memind ? 5'b00101 : 5'bz;  // Controlled_Buffer controlled_buffer_3
  assign Adr = regind ? 5'b01010 : 5'bz;  // Controlled_Buffer controlled_buffer_4
  assign Adr = postincr ? 5'b01011 : 5'bz;  // Controlled_Buffer controlled_buffer_5
  assign Adr = postdec ? 5'b01100 : 5'bz;  // Controlled_Buffer controlled_buffer_6
  assign Adr = regdir ? 5'b10010 : 5'bz;  // Controlled_Buffer controlled_buffer_7
endmodule

module KMOPR (
  input  HALT,
  input  RTS,
  input  RTI,
  input  ROTR,
  input  ROTRC,
  input  PUSH,
  input  POP,
  input  BLEQ,
  input  BGREU,
  input  BNNG,
  input  BGRT,
  input  JLEQ,
  input  JSR,
  input  JMP,
  input  LD,
  input  ST,
  input  ADD,
  input  INC,
  input  LOR,
  input  STRFIND,
  output [5:0] Adr
);

  assign Adr = HALT ? 6'b000010 : 6'bz;  // Controlled_Buffer controlled_buffer_1
  assign Adr = RTS ? 6'b000100 : 6'bz;  // Controlled_Buffer controlled_buffer_2
  assign Adr = RTI ? 6'b001010 : 6'bz;  // Controlled_Buffer controlled_buffer_3
  assign Adr = ROTR ? 6'b001100 : 6'bz;  // Controlled_Buffer controlled_buffer_4
  assign Adr = ROTRC ? 6'b001110 : 6'bz;  // Controlled_Buffer controlled_buffer_5
  assign Adr = PUSH ? 6'b010000 : 6'bz;  // Controlled_Buffer controlled_buffer_6
  assign Adr = POP ? 6'b010001 : 6'bz;  // Controlled_Buffer controlled_buffer_7
  assign Adr = BLEQ ? 6'b010010 : 6'bz;  // Controlled_Buffer controlled_buffer_8
  assign Adr = BGREU ? 6'b010111 : 6'bz;  // Controlled_Buffer controlled_buffer_9
  assign Adr = BNNG ? 6'b011110 : 6'bz;  // Controlled_Buffer controlled_buffer_10
  assign Adr = BGRT ? 6'b100010 : 6'bz;  // Controlled_Buffer controlled_buffer_11
  assign Adr = JLEQ ? 6'b100010 : 6'bz;  // Controlled_Buffer controlled_buffer_12
  assign Adr = JSR ? 6'b100010 : 6'bz;  // Controlled_Buffer controlled_buffer_13
  assign Adr = JMP ? 6'b100010 : 6'bz;  // Controlled_Buffer controlled_buffer_14
  assign Adr = LD ? 6'b100010 : 6'bz;  // Controlled_Buffer controlled_buffer_15
  assign Adr = ST ? 6'b100010 : 6'bz;  // Controlled_Buffer controlled_buffer_16
  assign Adr = ADD ? 6'b100010 : 6'bz;  // Controlled_Buffer controlled_buffer_17
  assign Adr = INC ? 6'b100010 : 6'bz;  // Controlled_Buffer controlled_buffer_18
  assign Adr = LOR ? 6'b100010 : 6'bz;  // Controlled_Buffer controlled_buffer_19
  assign Adr = STRFIND ? 6'b100010 : 6'bz;  // Controlled_Buffer controlled_buffer_20
endmodule
